// Logisim project DSFProjectSimulation.circ as structural Verilog: 1 circuit, main circuit main
module main (
);

  wire a14_out, a17_out, a20_out, and_1_out, and_2_out, and_3_out, and_4_out, and_5_out, and_6_out,
       and_7_out, and_8_out, and_9_out, and_10_out, and_11_out, and_12_out, and_13_out, and_14_out,
       and_15_out, and_16_out, and_17_out, and_18_out, and_19_out, and_20_out, and_21_out, and_22_out,
       and_23_out, and_24_out, and_25_out, and_26_out, and_27_out, and_28_out, and_29_out, and_30_out,
       and_31_out, B00_out, B01_out, B02_out, B03_out, B04_out, B05_out, B06_out, B07_out, B08_out, B09_out,
       clock_1_out, d_ff_1_q, d_ff_2_q, d_ff_3_q, d_ff_4_q, d_ff_5_q, d_ff_6_q, d_ff_7_q, d_ff_8_q, d_ff_9_q,
       d_ff_10_q, E1_q, E2_q, E3_q, E4_q, Green_FF_q, not_1_out, not_2_out, not_3_out, not_4_out, not_5_out,
       not_6_out, not_7_out, not_8_out, not_9_out, not_10_out, not_11_out, not_12_out, not_13_out,
       not_14_out, not_15_out, or_1_out, or_2_out, or_3_out, or_4_out, or_5_out, or_6_out, or_7_out,
       or_8_out, or_9_out, or_10_out, or_11_out, or_12_out, or_13_out, or_14_out, or_15_out, or_16_out,
       or_17_out, or_18_out, or_19_out, or_20_out, or_21_out, or_22_out, or_23_out, Red_FF_q, Reset_out,
       S0_q, S1_q, S1_qn, S2_q, S3_q, S4_q;

  Button B00 (.out(B00_out));
  Button B01 (.out(B01_out));
  Button B02 (.out(B02_out));
  Button B03 (.out(B03_out));
  Button B04 (.out(B04_out));
  Button B05 (.out(B05_out));
  Button B06 (.out(B06_out));
  Button B07 (.out(B07_out));
  Button B08 (.out(B08_out));
  Button B09 (.out(B09_out));
  Clock clock_1 (.out(clock_1_out));
  D_Flip_Flop d_ff_1 (.D(B00_out), .clk(clock_1_out), .Q(d_ff_1_q));  // open: Qn, preset, reset
  D_Flip_Flop d_ff_2 (.D(B01_out), .clk(clock_1_out), .Q(d_ff_2_q));  // open: Qn, preset, reset
  D_Flip_Flop d_ff_3 (.D(B02_out), .clk(clock_1_out), .Q(d_ff_3_q));  // open: Qn, preset, reset
  D_Flip_Flop d_ff_4 (.D(B03_out), .clk(clock_1_out), .Q(d_ff_4_q));  // open: Qn, preset, reset
  D_Flip_Flop d_ff_5 (.D(B04_out), .clk(clock_1_out), .Q(d_ff_5_q));  // open: Qn, preset, reset
  D_Flip_Flop d_ff_6 (.D(B05_out), .clk(clock_1_out), .Q(d_ff_6_q));  // open: Qn, preset, reset
  D_Flip_Flop d_ff_7 (.D(B06_out), .clk(clock_1_out), .Q(d_ff_7_q));  // open: Qn, preset, reset
  D_Flip_Flop d_ff_8 (.D(B07_out), .clk(clock_1_out), .Q(d_ff_8_q));  // open: Qn, preset, reset
  D_Flip_Flop d_ff_9 (.D(B08_out), .clk(clock_1_out), .Q(d_ff_9_q));  // open: Qn, preset, reset
  D_Flip_Flop d_ff_10 (.D(B09_out), .clk(clock_1_out), .Q(d_ff_10_q));  // open: Qn, preset, reset
  not not_1 (not_1_out, B00_out);
  not not_2 (not_2_out, B01_out);
  not not_3 (not_3_out, B02_out);
  not not_4 (not_4_out, B03_out);
  not not_5 (not_5_out, B04_out);
  not not_6 (not_6_out, B05_out);
  not not_7 (not_7_out, B06_out);
  not not_8 (not_8_out, B07_out);
  not not_9 (not_9_out, B08_out);
  not not_10 (not_10_out, B09_out);
  and and_1 (and_1_out, not_1_out, d_ff_1_q);
  and and_2 (and_2_out, not_2_out, d_ff_2_q);
  and and_3 (and_3_out, not_3_out, d_ff_3_q);
  and and_4 (and_4_out, not_4_out, d_ff_4_q);
  and and_5 (and_5_out, not_5_out, d_ff_5_q);
  and and_6 (and_6_out, not_6_out, d_ff_6_q);
  and and_7 (and_7_out, not_7_out, d_ff_7_q);
  and and_8 (and_8_out, not_8_out, d_ff_8_q);
  and and_9 (and_9_out, not_9_out, d_ff_9_q);
  and and_10 (and_10_out, not_10_out, d_ff_10_q);
  or or_1 (or_1_out, and_1_out, and_2_out, and_3_out, and_4_out, and_5_out, and_6_out, and_7_out, and_8_out, and_9_out, and_10_out);
  not not_11 (not_11_out, or_1_out);
  not not_12 (not_12_out, and_5_out);
  not not_13 (not_13_out, and_6_out);
  not not_14 (not_14_out, and_3_out);
  and and_11 (and_11_out, S0_q, and_5_out);
  and and_12 (and_12_out, not_11_out, S1_q);
  and and_13 (and_13_out, S2_q, and_3_out);
  and and_14 (and_14_out, not_11_out, S3_q);
  and and_15 (and_15_out, S3_q, and_3_out);
  and and_16 (and_16_out, not_11_out, S4_q);
  or or_2 (or_2_out, and_11_out, and_12_out);
  or or_3 (or_3_out, and_13_out, and_14_out);
  or or_4 (or_4_out, and_15_out, and_16_out);
  and and_17 (and_17_out, S1_q, or_1_out, not_13_out);
  and a14 (a14_out, or_1_out, E1_q);
  or or_5 (or_5_out, and_17_out, a14_out, and_18_out);
  and and_18 (and_18_out, not_11_out, E2_q);
  and and_19 (and_19_out, S3_q, not_14_out, or_1_out);
  and a20 (a20_out, or_1_out, E3_q);
  and and_20 (and_20_out, E4_q, not_11_out);
  or or_6 (or_6_out, E4_q, S4_q);
  or or_7 (or_7_out, and_19_out, a20_out, and_20_out);
  and and_21 (and_21_out, S0_q, not_11_out);
  and and_22 (and_22_out, or_1_out, or_6_out);
  and and_23 (and_23_out, S1_q, and_6_out);
  and and_24 (and_24_out, not_11_out, S2_q);
  and and_25 (and_25_out, S0_q, not_12_out, or_1_out);
  and and_26 (and_26_out, not_11_out, E1_q);
  and and_27 (and_27_out, S2_q, or_1_out, not_14_out);
  and a17 (a17_out, or_1_out, E2_q);
  and and_28 (and_28_out, not_11_out, E3_q);
  or or_8 (or_8_out, and_21_out, and_22_out);
  or or_9 (or_9_out, and_23_out, and_24_out);
  or or_10 (or_10_out, and_25_out, and_26_out);
  or or_11 (or_11_out, and_27_out, a17_out, and_28_out);
  D_Flip_Flop S0 (.D(or_8_out), .clk(clock_1_out), .Q(S0_q), .preset(Reset_out));  // open: Qn, reset
  D_Flip_Flop S1 (.D(or_2_out), .clk(clock_1_out), .Q(S1_q), .Qn(S1_qn), .reset(Reset_out));  // open: preset
  D_Flip_Flop S2 (.D(or_9_out), .clk(clock_1_out), .Q(S2_q), .Qn(S1_qn), .reset(Reset_out));  // open: preset
  D_Flip_Flop S3 (.D(or_3_out), .clk(clock_1_out), .Q(S3_q), .Qn(S1_qn), .reset(Reset_out));  // open: preset
  D_Flip_Flop S4 (.D(or_4_out), .clk(clock_1_out), .Q(S4_q), .Qn(S1_qn), .reset(Reset_out));  // open: preset
  D_Flip_Flop E1 (.D(or_10_out), .clk(clock_1_out), .Q(E1_q), .Qn(S1_qn), .reset(Reset_out));  // open: preset
  D_Flip_Flop E2 (.D(or_5_out), .clk(clock_1_out), .Q(E2_q), .Qn(S1_qn), .reset(Reset_out));  // open: preset
  D_Flip_Flop E3 (.D(or_11_out), .clk(clock_1_out), .Q(E3_q), .Qn(S1_qn), .reset(Reset_out));  // open: preset
  D_Flip_Flop E4 (.D(or_7_out), .clk(clock_1_out), .Q(E4_q), .Qn(S1_qn), .reset(Reset_out));  // open: preset
  not not_15 (not_15_out, and_2_out);
  Button Reset (.out(Reset_out));
  and and_29 (and_29_out, or_1_out, E4_q);
  and and_30 (and_30_out, S4_q, or_1_out, not_15_out);
  and and_31 (and_31_out, S4_q, and_2_out);
  or or_12 (or_12_out, and_29_out, and_30_out);
  or or_13 (or_13_out, Green_FF_q, and_31_out);
  or or_14 (or_14_out, S2_q, E2_q, or_15_out);
  or or_15 (or_15_out, S3_q, E3_q, or_16_out);
  or or_16 (or_16_out, S4_q, E4_q);
  or or_17 (or_17_out, Red_FF_q, or_12_out);
  D_Flip_Flop Red_FF (.D(or_17_out), .clk(clock_1_out), .Q(Red_FF_q), .reset(Reset_out));  // open: Qn, preset
  D_Flip_Flop Green_FF (.D(or_13_out), .clk(clock_1_out), .Q(Green_FF_q), .reset(Reset_out));  // open: Qn, preset
  or or_18 (or_18_out, S1_q, E1_q, or_14_out);
  or or_19 (or_19_out, Red_FF_q, Green_FF_q);
  LED Red (.in(Red_FF_q));
  LED Green (.in(Green_FF_q));
  or or_20 (or_20_out, or_18_out, or_19_out);
  LED Input_1 (.in(or_20_out));
  or or_21 (or_21_out, or_14_out, or_19_out);
  LED Input_2 (.in(or_21_out));
  or or_22 (or_22_out, or_15_out, or_19_out);
  LED Input_3 (.in(or_22_out));
  or or_23 (or_23_out, or_16_out, or_19_out);
  LED Input_4 (.in(or_23_out));
  LED Input_5 (.in(or_19_out));

  // Notes on the sheet:
  //   q1
  //   q2
  //   q3
  //   q4
  //   q5
  //   q6
  //   q7
  //   q8
  //   q9
  //   q0
  //   c0
  //   c5
  //   c6
  //   c7
  //   c8
  //   c9
  //   c1
  //   c2
  //   c3
  //   c4
  //   Press
  //   a3
  //   a4
  //   a7
  //   a8
  //   a9
  //   a10
  //   o3
  //   o5
  //   o6
  //   a13
  //   o8
  //   a15
  //   a19
  //   a21
  //   o2
  //   o10
  //   a1
  //   a2
  //   a5
  //   a11
  //   a12
  //   a16
  //   a18
  //   o1
  //   o4
  //   a6
  //   o7
  //   o9
  //   reset/!reset
endmodule
